# Fritzing sketch arduino_countdown (saved by Fritzing 0.8.3b)
breadboards: 1

parts:
  Arduino1 = Arduino
  S1 = Pushbutton [package="[THT]"]
  R1 = Resistor [tolerance=±5% resistance=1k package=THT]
  R2 = Rotary Potentiometer (Small) [maximum_resistance=100kΩ]
  J1 = Piezo Speaker
  7_Segment1 = 3 digits 7 Segment Display
  R3 = Resistor [tolerance=±5% resistance=1k package=THT]
  R4 = Resistor [tolerance=±5% resistance=1k package=THT]
  R5 = Resistor [tolerance=±5% resistance=1k package=THT]

nets:
  N1: Arduino1.D13, S1.Pin_3, S1.Pin_4, R1.Pin_1
  N2: Arduino1.D12, R3.Pin_0
  N3: Arduino1.D11, R4.Pin_0
  N4: Arduino1.D10, R5.Pin_0
  N5: Arduino1.D9, 7_Segment1.Segment_B
  N6: Arduino1.D8, 7_Segment1.Segment_A
  N7: Arduino1.D7, 7_Segment1.Segment_DP
  N8: Arduino1.D6, 7_Segment1.Segment_G
  N9: Arduino1.D5, 7_Segment1.Segment_F
  N10: Arduino1.D4, 7_Segment1.Segment_E
  N11: Arduino1.D3, 7_Segment1.Segment_D
  N12: Arduino1.D2, 7_Segment1.Segment_C
  N13: Arduino1.D1TX, J1.pin2
  N14: Arduino1.+5V, R1.Pin_0, R2.leg1
  N15: Arduino1.GND, S1.Pin_1, S1.Pin_2, R2.leg2, J1.pin1
  N16: Arduino1.A0, R2.wiper
  N17: 7_Segment1.common_cathode_1, R3.Pin_1
  N18: 7_Segment1.common_cathode_2, R4.Pin_1
  N19: 7_Segment1.common_cathode_3, R5.Pin_1

custom parts:
  3 digits 7 Segment Display: 7 Segment Display with common cathode.
